// Logisim project datapath.circ as structural Verilog: 1 circuit, main circuit main
module main (
  input  Cin,
  input  Binvert,
  input  in_3,
  input  MemotoReg,
  input  RegDes,
  input  store,
  input  load,
  input  ALUSrc,
  input  Write_Control_Signal,
  output [15:0] out_10,
  output [15:0] Output,
  output [1:0] out_12,
  output [15:0] out_13,
  output [3:0] out_14,
  output [3:0] out_15,
  output [3:0] out_16,
  output [3:0] out_17,
  output Overflow,
  output Zero_Flag,
  output [15:0] out_20,
  output [15:0] out_21
);

  wire Clock_out, Reset_2_out, Reset_out;
  wire [3:2] ram_1_data;
  wire [15:0] adder_1_out, bit_extender_1_out, main_1_read_data_2, register_1_q;

  Adder #(.width(16)) adder_1 (.a(16'hfffe), .b(register_1_q), .out(adder_1_out));  // open: cin, cout
  Register #(.width(16)) register_1 (.D(adder_1_out), .Q(register_1_q), .clk(Clock_out), .clr(Reset_out));  // open: en
  Button Reset (.out(Reset_out));
  Clock Clock (.out(Clock_out));
  RAM #(.addrWidth(16), .dataWidth(16)) ram_1 (
    .addr(register_1_q), .data({out_17, out_15, out_14, ram_1_data, out_12}), .ld(in_3));  // open: sel, clk, clr
  Multiplexer #(.width(4)) multiplexer_1 (.in0(out_15), .in1(out_17), .out(out_16), .sel(RegDes));  // open: en
  assign bit_extender_1_out = {{12{1'b0}}, out_17};  // Bit_Extender bit_extender_1
  Register_main main_1 (
    .Write_Register(out_16), .Wrtie_Control(Write_Control_Signal), .Clock(Clock_out), .Write_Datas(out_20),
    .Read_Data_1(out_13), .Read_Register_1(out_14), .Read_Data_2(main_1_read_data_2), .Read_Register_2(out_15));
  Multiplexer #(.width(16)) multiplexer_2 (
    .in0(main_1_read_data_2), .in1(bit_extender_1_out), .out(out_21), .sel(ALUSrc));  // open: en
  ALU_main main_2 (
    .A(out_13), .B(out_21), .Binvert(Binvert), .OPERATION(out_12), .CIN(Cin), .Output(Output),
    .Zero_Sign(Zero_Flag), .Over_Flow(Overflow));
  RAM #(.addrWidth(16), .dataWidth(16), .bus("separate")) ram_2 (
    .addr(out_13), .din(Output), .data(out_10), .str(store), .clk(Clock_out), .ld(load), .clr(Reset_2_out));  // open: sel
  Button Reset_2 (.out(Reset_2_out));
  Multiplexer #(.width(16)) multiplexer_3 (.in0(Output), .in1(out_10), .out(out_20), .sel(MemotoReg));  // open: en
endmodule
