// Logisim project alu.circ as structural Verilog: 2 circuits, main circuit main
module main (
  input  Binvert,
  input  [1:0] OPERATION,
  input  CIN,
  input  [15:0] A,
  input  [15:0] B,
  output [15:0] Output,
  output Zero_Sign,
  output Over_Flow
);

  wire n1_bit_alu_1_cout, n1_bit_alu_2_cout, n1_bit_alu_3_cout, n1_bit_alu_4_cout, n1_bit_alu_5_cout,
       n1_bit_alu_6_cout, n1_bit_alu_7_cout, n1_bit_alu_8_cout, n1_bit_alu_9_cout, n1_bit_alu_10_cout,
       n1_bit_alu_11_cout, n1_bit_alu_12_cout, n1_bit_alu_13_cout, n1_bit_alu_14_cout, n1_bit_alu_15_cout;

  _1_bit_alu u_1_bit_alu_1 (
    .Binvert(Binvert), .Output(Output[0]), .COUT(n1_bit_alu_1_cout), .A(A[0]), .B(B[0]), .CIN(CIN),
    .S(OPERATION));
  _1_bit_alu u_1_bit_alu_2 (
    .Binvert(Binvert), .Output(Output[1]), .COUT(n1_bit_alu_2_cout), .A(A[1]), .B(B[1]),
    .CIN(n1_bit_alu_1_cout), .S(OPERATION));
  _1_bit_alu u_1_bit_alu_3 (
    .Binvert(Binvert), .Output(Output[2]), .COUT(n1_bit_alu_3_cout), .A(A[2]), .B(B[2]),
    .CIN(n1_bit_alu_2_cout), .S(OPERATION));
  _1_bit_alu u_1_bit_alu_4 (
    .Binvert(Binvert), .Output(Output[3]), .COUT(n1_bit_alu_4_cout), .A(A[3]), .B(B[3]),
    .CIN(n1_bit_alu_3_cout), .S(OPERATION));
  _1_bit_alu u_1_bit_alu_5 (
    .Binvert(Binvert), .Output(Output[4]), .COUT(n1_bit_alu_5_cout), .A(A[4]), .B(B[4]),
    .CIN(n1_bit_alu_4_cout), .S(OPERATION));
  _1_bit_alu u_1_bit_alu_6 (
    .Binvert(Binvert), .Output(Output[5]), .COUT(n1_bit_alu_6_cout), .A(A[5]), .B(B[5]),
    .CIN(n1_bit_alu_5_cout), .S(OPERATION));
  _1_bit_alu u_1_bit_alu_7 (
    .Binvert(Binvert), .Output(Output[6]), .COUT(n1_bit_alu_7_cout), .A(A[6]), .B(B[6]),
    .CIN(n1_bit_alu_6_cout), .S(OPERATION));
  _1_bit_alu u_1_bit_alu_8 (
    .Binvert(Binvert), .Output(Output[7]), .COUT(n1_bit_alu_8_cout), .A(A[7]), .B(B[7]),
    .CIN(n1_bit_alu_7_cout), .S(OPERATION));
  _1_bit_alu u_1_bit_alu_9 (
    .Binvert(Binvert), .Output(Output[8]), .COUT(n1_bit_alu_9_cout), .A(A[8]), .B(B[8]),
    .CIN(n1_bit_alu_8_cout), .S(OPERATION));
  _1_bit_alu u_1_bit_alu_10 (
    .Binvert(Binvert), .Output(Output[9]), .COUT(n1_bit_alu_10_cout), .A(A[9]), .B(B[9]),
    .CIN(n1_bit_alu_9_cout), .S(OPERATION));
  _1_bit_alu u_1_bit_alu_11 (
    .Binvert(Binvert), .Output(Output[10]), .COUT(n1_bit_alu_11_cout), .A(A[10]), .B(B[10]),
    .CIN(n1_bit_alu_10_cout), .S(OPERATION));
  _1_bit_alu u_1_bit_alu_12 (
    .Binvert(Binvert), .Output(Output[11]), .COUT(n1_bit_alu_12_cout), .A(A[11]), .B(B[11]),
    .CIN(n1_bit_alu_11_cout), .S(OPERATION));
  _1_bit_alu u_1_bit_alu_13 (
    .Binvert(Binvert), .Output(Output[12]), .COUT(n1_bit_alu_13_cout), .A(A[12]), .B(B[12]),
    .CIN(n1_bit_alu_12_cout), .S(OPERATION));
  _1_bit_alu u_1_bit_alu_14 (
    .Binvert(Binvert), .Output(Output[13]), .COUT(n1_bit_alu_14_cout), .A(A[13]), .B(B[13]),
    .CIN(n1_bit_alu_13_cout), .S(OPERATION));
  _1_bit_alu u_1_bit_alu_15 (
    .Binvert(Binvert), .Output(Output[14]), .COUT(n1_bit_alu_15_cout), .A(A[14]), .B(B[14]),
    .CIN(n1_bit_alu_14_cout), .S(OPERATION));
  _1_bit_alu u_1_bit_alu_16 (
    .Binvert(Binvert), .Output(Output[15]), .COUT(Over_Flow), .A(A[15]), .B(B[15]), .CIN(n1_bit_alu_15_cout),
    .S(OPERATION));
  nor nor_1 (Zero_Sign, Output[0], Output[1], Output[2], Output[3], Output[4], Output[5], Output[6], Output[8], Output[9], Output[10], Output[11], Output[12], Output[13], Output[14], Output[15], Output[7]);
endmodule

module _1_bit_alu (
  input  A,
  input  B,
  input  CIN,
  input  [1:0] S,
  input  Binvert,
  output Output,
  output COUT
);

  wire adder_1_out, and_1_out, multiplexer_1_out, not_1_out, or_1_out;

  not not_1 (not_1_out, B);
  Multiplexer multiplexer_1 (.in0(B), .in1(not_1_out), .out(multiplexer_1_out), .sel(Binvert));  // open: en
  and and_1 (and_1_out, B, A);
  or or_1 (or_1_out, B, A);
  Adder #(.width(1)) adder_1 (.a(A), .b(multiplexer_1_out), .out(adder_1_out), .cin(CIN), .cout(COUT));
  Multiplexer #(.select(2)) multiplexer_2 (
    .in0(and_1_out), .in1(or_1_out), .in2(adder_1_out), .out(Output), .sel(S));  // open: in3, en
endmodule
