// Logisim project pipelined_datapath(unsure).circ as structural Verilog: 2 circuits, main circuit main
module main (
  input  Binvert,
  input  Cin,
  input  in_3,
  input  MemtoReg,
  input  store,
  input  load,
  input  RegDst,
  input  Write_Control_Signal,
  input  ALUSrc,
  output [15:0] out_10,
  output [1:0] out_11,
  output [15:0] \output ,
  output [15:0] out_13,
  output [15:0] out_14,
  output [3:0] out_15,
  output [3:0] out_16,
  output [15:0] out_17,
  output [3:0] out_18,
  output Overflow,
  output Zero_Flag,
  output [15:0] out_21,
  output [15:0] out_22
);

  wire Clock_out, Reset_2_out, Reset_out;
  wire [3:0] multiplexer_1_out;
  wire [15:0] adder_1_out, main_1_read_data_1, main_2_output, pipeline_2_out_9, pipeline_2_out_11,
       pipeline_3_out_11, pipeline_4_out_9, ram_1_data, ram_2_data, register_1_q;
  wire [15:14] pipeline_1_out_7;

  Button Reset (.out(Reset_out));
  Register #(.width(16)) register_1 (.D(adder_1_out), .Q(register_1_q), .clk(Clock_out), .clr(Reset_out));  // open: en
  Adder #(.width(16)) adder_1 (.a(16'h1), .b(register_1_q), .out(adder_1_out));  // open: cin, cout
  RAM #(.addrWidth(16), .dataWidth(16)) ram_1 (
    .addr(register_1_q), .data(ram_1_data), .ld(in_3));  // open: sel, clk, clr
  Pipeline pipeline_1 (
    .in_1(ram_1_data), .clock(Clock_out), .out_7({pipeline_1_out_7, out_11, out_16, out_15, out_18}));  // open: in_2, in_3, in_4, in_5, out_8, out_9, out_10, out_11
  Clock Clock (.out(Clock_out));
  Multiplexer #(.width(4)) multiplexer_1 (
    .in0(out_15), .in1(out_18), .out(multiplexer_1_out), .sel(RegDst));  // open: en
  assign out_22 = {{12{1'b0}}, out_18};  // Bit_Extender bit_extender_1
  register_main main_1 (
    .Write_Register(multiplexer_1_out), .Wrtie_Control(Write_Control_Signal), .Clock(Clock_out),
    .Read_Data_1(main_1_read_data_1), .Read_Register_1(out_16), .Read_Data_2(out_10), .Read_Register_2(out_15));  // open: Write_Datas
  Pipeline pipeline_2 (
    .in_1(main_1_read_data_1), .in_5(out_22), .clock(Clock_out), .out_7(out_14), .out_9(pipeline_2_out_9),
    .out_11(pipeline_2_out_11));  // open: in_2, in_3, in_4, out_8, out_10
  Multiplexer #(.width(16)) multiplexer_2 (
    .in0(pipeline_2_out_9), .in1(pipeline_2_out_11), .out(out_21), .sel(ALUSrc));  // open: en
  alu_main main_2 (
    .A(out_14), .B(out_21), .Binvert(Binvert), .OPERATION(out_11), .CIN(Cin), .Output(main_2_output),
    .Zero_Sign(Zero_Flag), .Over_Flow(Overflow));
  Pipeline pipeline_3 (
    .in_1(main_2_output), .in_5(out_14), .clock(Clock_out), .out_7(\output ), .out_11(pipeline_3_out_11));  // open: in_2, in_3, in_4, out_8, out_9, out_10
  RAM #(.addrWidth(16), .dataWidth(16), .bus("separate")) ram_2 (
    .addr(pipeline_3_out_11), .din(\output ), .data(ram_2_data), .str(store), .clk(Clock_out), .ld(load),
    .clr(Reset_2_out));  // open: sel
  Button Reset_2 (.out(Reset_2_out));
  Pipeline pipeline_4 (
    .in_1(\output ), .in_3(ram_2_data), .clock(Clock_out), .out_7(out_13), .out_9(pipeline_4_out_9));  // open: in_2, in_4, in_5, out_8, out_10, out_11
  Multiplexer #(.width(16)) multiplexer_3 (
    .in0(out_13), .in1(pipeline_4_out_9), .out(out_17), .sel(MemtoReg));  // open: en
endmodule

module Pipeline (
  input  [15:0] in_1,
  input  [15:0] in_2,
  input  [15:0] in_3,
  input  [15:0] in_4,
  input  [15:0] in_5,
  input  clock,
  output [15:0] out_7,
  output [15:0] out_8,
  output [15:0] out_9,
  output [15:0] out_10,
  output [15:0] out_11
);

  Register #(.width(16)) register_1 (.D(in_1), .Q(out_7), .clk(clock));  // open: en, clr
  Register #(.width(16)) register_2 (.D(in_2), .Q(out_8), .clk(clock));  // open: en, clr
  Register #(.width(16)) register_3 (.D(in_3), .Q(out_9), .clk(clock));  // open: en, clr
  Register #(.width(16)) register_4 (.D(in_4), .Q(out_10), .clk(clock));  // open: en, clr
  Register #(.width(16)) register_5 (.D(in_5), .Q(out_11), .clk(clock));  // open: en, clr
endmodule
