// Logisim project 4 Digit Lock.circ as structural Verilog: 3 circuits, main circuit main
module main (
  input  _0,
  input  _1,
  input  _2,
  input  _3,
  input  _4,
  input  _5,
  input  _6,
  input  _7,
  input  _8,
  input  _9,
  input  Mode
);

  wire and_1_out, Clock_out, comparator_1_eq, comparator_2_eq, comparator_3_eq, comparator_4_eq,
       comparator_5_eq, comparator_6_eq, comparator_7_eq, comparator_8_eq, comparator_9_eq, comparator_10_eq,
       comparator_11_eq, comparator_12_eq, comparator_13_eq, comparator_14_eq, comparator_16_eq,
       D1_Decoder_2_a_2, D1_Decoder_2_b_2, D1_Decoder_2_c_2, D1_Decoder_2_d_2, D1_Decoder_2_e,
       D1_Decoder_2_f, D1_Decoder_2_g, D1_Decoder_3_a_2, D1_Decoder_3_b_2, D1_Decoder_3_c_2,
       D1_Decoder_3_d_2, D1_Decoder_3_e, D1_Decoder_3_f, D1_Decoder_3_g, D1_Decoder_4_a_2, D1_Decoder_4_b_2,
       D1_Decoder_4_c_2, D1_Decoder_4_d_2, D1_Decoder_4_e, D1_Decoder_4_f, D1_Decoder_4_g, D1_Decoder_a_2,
       D1_Decoder_b_2, D1_Decoder_c_2, D1_Decoder_d_2, D1_Decoder_e, D1_Decoder_f, D1_Decoder_g,
       D2_Decoder_a, D2_Decoder_b, D2_Decoder_c, D2_Decoder_d, D2_Decoder_e, D2_Decoder_f, D2_Decoder_g,
       d_ff_1_q, d_ff_2_q, d_ff_3_q, d_ff_4_q, d_ff_5_q, d_ff_6_q, d_ff_7_q, d_ff_8_q, d_ff_9_q, d_ff_10_q,
       d_ff_11_q, d_ff_12_q, d_ff_13_q, d_ff_14_q, d_ff_15_q, d_ff_16_q, d_ff_17_q, d_ff_18_q, d_ff_19_q,
       d_ff_20_q, d_ff_21_q, d_ff_22_q, d_ff_23_q, d_ff_24_q, d_ff_25_q, d_ff_26_q, d_ff_27_q, d_ff_28_q,
       d_ff_29_q, d_ff_30_q, d_ff_31_q, d_ff_32_q, not_1_out, or_1_out;
  wire [3:0] priority_encoder_1_out;

  Clock Clock (.out(Clock_out));
  Priority_Encoder #(.select(4)) priority_encoder_1 (
    .in0(_0), .in1(_1), .in2(_2), .in3(_3), .in4(_4), .in5(_5), .in6(_6), .in7(_7), .in8(_8), .in9(_9),
    .out(priority_encoder_1_out), .en_in(or_1_out));  // open: in10, in11, in12, in13, in14, in15, gs, en_out
  not not_1 (not_1_out, Mode);
  or or_1 (or_1_out, Mode, not_1_out);
  _7_Segment_Display u_7_segment_display_1 (
    .g(D1_Decoder_2_g), .f(D1_Decoder_2_f), .a(D1_Decoder_2_a_2), .b(D1_Decoder_2_b_2), .e(D1_Decoder_2_e),
    .d(D1_Decoder_2_d_2), .c(D1_Decoder_2_c_2));  // open: dp
  _7_Segment_Display u_7_segment_display_2 (
    .g(D1_Decoder_g), .f(D1_Decoder_f), .a(D1_Decoder_a_2), .b(D1_Decoder_b_2), .e(D1_Decoder_e),
    .d(D1_Decoder_d_2), .c(D1_Decoder_c_2));  // open: dp
  D_Flip_Flop d_ff_1 (
    .clk(Clock_out), .D(priority_encoder_1_out[3]), .Q(d_ff_1_q), .en(not_1_out));  // open: Qn, preset, reset
  D_Flip_Flop d_ff_2 (.clk(Clock_out), .D(d_ff_1_q), .Q(d_ff_2_q), .en(not_1_out));  // open: Qn, preset, reset
  D_Flip_Flop d_ff_3 (.clk(Clock_out), .D(d_ff_2_q), .Q(d_ff_3_q), .en(not_1_out));  // open: Qn, preset, reset
  D_Flip_Flop d_ff_4 (.clk(Clock_out), .D(d_ff_3_q), .Q(d_ff_4_q), .en(not_1_out));  // open: Qn, preset, reset
  _7_Segment_Display u_7_segment_display_3 (
    .g(D1_Decoder_3_g), .f(D1_Decoder_3_f), .a(D1_Decoder_3_a_2), .b(D1_Decoder_3_b_2), .e(D1_Decoder_3_e),
    .d(D1_Decoder_3_d_2), .c(D1_Decoder_3_c_2));  // open: dp
  _7_Segment_Display u_7_segment_display_4 (
    .g(D1_Decoder_4_g), .f(D1_Decoder_4_f), .a(D1_Decoder_4_a_2), .b(D1_Decoder_4_b_2), .e(D1_Decoder_4_e),
    .d(D1_Decoder_4_d_2), .c(D1_Decoder_4_c_2));  // open: dp
  _7_Segment_Display u_7_segment_display_5 (
    .g(D2_Decoder_g), .f(D2_Decoder_f), .a(D2_Decoder_a), .b(D2_Decoder_b), .e(D2_Decoder_e),
    .d(D2_Decoder_d), .c(D2_Decoder_c));  // open: dp
  D_Flip_Flop d_ff_5 (
    .clk(Clock_out), .D(priority_encoder_1_out[2]), .Q(d_ff_5_q), .en(not_1_out));  // open: Qn, preset, reset
  D_Flip_Flop d_ff_6 (.clk(Clock_out), .D(d_ff_5_q), .Q(d_ff_6_q), .en(not_1_out));  // open: Qn, preset, reset
  D_Flip_Flop d_ff_7 (.clk(Clock_out), .D(d_ff_6_q), .Q(d_ff_7_q));  // open: Qn, preset, en, reset
  D_Flip_Flop d_ff_8 (.clk(Clock_out), .D(d_ff_7_q), .Q(d_ff_8_q), .en(not_1_out));  // open: Qn, preset, reset
  D_Flip_Flop d_ff_9 (
    .clk(Clock_out), .D(priority_encoder_1_out[1]), .Q(d_ff_9_q), .en(not_1_out));  // open: Qn, preset, reset
  D_Flip_Flop d_ff_10 (.clk(Clock_out), .D(d_ff_9_q), .Q(d_ff_10_q), .en(not_1_out));  // open: Qn, preset, reset
  D_Flip_Flop d_ff_11 (.clk(Clock_out), .D(d_ff_10_q), .Q(d_ff_11_q), .en(not_1_out));  // open: Qn, preset, reset
  D_Flip_Flop d_ff_12 (.clk(Clock_out), .D(d_ff_11_q), .Q(d_ff_12_q), .en(not_1_out));  // open: Qn, preset, reset
  Comparator #(.width(1)) comparator_1 (.a(d_ff_1_q), .b(d_ff_17_q), .eq(comparator_1_eq));  // open: gt, lt
  Comparator #(.width(1)) comparator_2 (.a(d_ff_2_q), .b(d_ff_18_q), .eq(comparator_2_eq));  // open: gt, lt
  Comparator #(.width(1)) comparator_3 (.a(d_ff_3_q), .b(d_ff_19_q), .eq(comparator_3_eq));  // open: gt, lt
  Comparator #(.width(1)) comparator_4 (.a(d_ff_4_q), .b(d_ff_20_q), .eq(comparator_4_eq));  // open: gt, lt
  D_Flip_Flop d_ff_13 (
    .clk(Clock_out), .D(priority_encoder_1_out[0]), .Q(d_ff_13_q), .en(not_1_out));  // open: Qn, preset, reset
  D_Flip_Flop d_ff_14 (.clk(Clock_out), .D(d_ff_13_q), .Q(d_ff_14_q), .en(not_1_out));  // open: Qn, preset, reset
  D_Flip_Flop d_ff_15 (.clk(Clock_out), .D(d_ff_14_q), .Q(d_ff_15_q), .en(not_1_out));  // open: Qn, preset, reset
  D_Flip_Flop d_ff_16 (.clk(Clock_out), .D(d_ff_15_q), .Q(d_ff_16_q), .en(not_1_out));  // open: Qn, preset, reset
  Comparator #(.width(1)) comparator_5 (.a(d_ff_5_q), .b(d_ff_21_q), .eq(comparator_5_eq));  // open: gt, lt
  Comparator #(.width(1)) comparator_6 (.a(d_ff_6_q), .b(d_ff_22_q), .eq(comparator_6_eq));  // open: gt, lt
  Comparator #(.width(1)) comparator_7 (.a(d_ff_7_q), .b(d_ff_23_q), .eq(comparator_7_eq));  // open: gt, lt
  Comparator #(.width(1)) comparator_8 (.a(d_ff_8_q), .b(d_ff_24_q), .eq(comparator_8_eq));  // open: gt, lt
  Display1_Decoder D1_Decoder (
    .D(d_ff_17_q), .C(d_ff_21_q), .B(d_ff_25_q), .A(d_ff_29_q), .a_2(D1_Decoder_a_2), .b_2(D1_Decoder_b_2),
    .c_2(D1_Decoder_c_2), .d_2(D1_Decoder_d_2), .e(D1_Decoder_e), .f(D1_Decoder_f), .g(D1_Decoder_g));
  D_Flip_Flop d_ff_17 (
    .clk(Clock_out), .D(priority_encoder_1_out[3]), .Q(d_ff_17_q), .en(Mode));  // open: Qn, preset, reset
  D_Flip_Flop d_ff_18 (.clk(Clock_out), .D(d_ff_17_q), .Q(d_ff_18_q), .en(Mode));  // open: Qn, preset, reset
  D_Flip_Flop d_ff_19 (.clk(Clock_out), .D(d_ff_18_q), .Q(d_ff_19_q), .en(Mode));  // open: Qn, preset, reset
  D_Flip_Flop d_ff_20 (.clk(Clock_out), .D(d_ff_19_q), .Q(d_ff_20_q), .en(Mode));  // open: Qn, preset, reset
  Comparator #(.width(1)) comparator_9 (.a(d_ff_9_q), .b(d_ff_25_q), .eq(comparator_9_eq));  // open: gt, lt
  Comparator #(.width(1)) comparator_10 (.a(d_ff_10_q), .b(d_ff_26_q), .eq(comparator_10_eq));  // open: gt, lt
  Comparator #(.width(1)) comparator_11 (.a(d_ff_11_q), .b(d_ff_27_q), .eq(comparator_11_eq));  // open: gt, lt
  Comparator #(.width(1)) comparator_12 (.a(d_ff_12_q), .b(d_ff_28_q), .eq(comparator_12_eq));  // open: gt, lt
  Display1_Decoder D1_Decoder_2 (
    .D(d_ff_18_q), .C(d_ff_22_q), .B(d_ff_26_q), .A(d_ff_30_q), .a_2(D1_Decoder_2_a_2),
    .b_2(D1_Decoder_2_b_2), .c_2(D1_Decoder_2_c_2), .d_2(D1_Decoder_2_d_2), .e(D1_Decoder_2_e),
    .f(D1_Decoder_2_f), .g(D1_Decoder_2_g));
  D_Flip_Flop d_ff_21 (
    .clk(Clock_out), .D(priority_encoder_1_out[2]), .Q(d_ff_21_q), .en(Mode));  // open: Qn, preset, reset
  D_Flip_Flop d_ff_22 (.clk(Clock_out), .D(d_ff_21_q), .Q(d_ff_22_q), .en(Mode));  // open: Qn, preset, reset
  D_Flip_Flop d_ff_23 (.clk(Clock_out), .D(d_ff_22_q), .Q(d_ff_23_q), .en(Mode));  // open: Qn, preset, reset
  D_Flip_Flop d_ff_24 (.clk(Clock_out), .D(d_ff_23_q), .Q(d_ff_24_q), .en(Mode));  // open: Qn, preset, reset
  Comparator #(.width(1)) comparator_13 (.a(d_ff_13_q), .b(d_ff_29_q), .eq(comparator_13_eq));  // open: gt, lt
  Comparator #(.width(1)) comparator_14 (.a(d_ff_14_q), .b(d_ff_30_q), .eq(comparator_14_eq));  // open: gt, lt
  Comparator #(.width(1)) comparator_15 (.a(d_ff_15_q), .b(d_ff_31_q));  // open: gt, eq, lt
  Comparator #(.width(1)) comparator_16 (.a(d_ff_16_q), .b(d_ff_32_q), .eq(comparator_16_eq));  // open: gt, lt
  Display1_Decoder D1_Decoder_3 (
    .D(d_ff_19_q), .C(d_ff_23_q), .B(d_ff_27_q), .A(d_ff_31_q), .a_2(D1_Decoder_3_a_2),
    .b_2(D1_Decoder_3_b_2), .c_2(D1_Decoder_3_c_2), .d_2(D1_Decoder_3_d_2), .e(D1_Decoder_3_e),
    .f(D1_Decoder_3_f), .g(D1_Decoder_3_g));
  D_Flip_Flop d_ff_25 (
    .clk(Clock_out), .D(priority_encoder_1_out[1]), .Q(d_ff_25_q), .en(Mode));  // open: Qn, preset, reset
  D_Flip_Flop d_ff_26 (.clk(Clock_out), .D(d_ff_25_q), .Q(d_ff_26_q));  // open: Qn, preset, en, reset
  D_Flip_Flop d_ff_27 (.clk(Clock_out), .D(d_ff_26_q), .Q(d_ff_27_q), .en(Mode));  // open: Qn, preset, reset
  D_Flip_Flop d_ff_28 (.clk(Clock_out), .D(d_ff_27_q), .Q(d_ff_28_q), .en(Mode));  // open: Qn, preset, reset
  Display1_Decoder D1_Decoder_4 (
    .D(d_ff_20_q), .C(d_ff_24_q), .B(d_ff_28_q), .A(d_ff_32_q), .a_2(D1_Decoder_4_a_2),
    .b_2(D1_Decoder_4_b_2), .c_2(D1_Decoder_4_c_2), .d_2(D1_Decoder_4_d_2), .e(D1_Decoder_4_e),
    .f(D1_Decoder_4_f), .g(D1_Decoder_4_g));
  and and_1 (and_1_out, comparator_1_eq, comparator_5_eq, comparator_9_eq, comparator_13_eq, comparator_2_eq, comparator_3_eq, comparator_4_eq, comparator_6_eq, comparator_14_eq, comparator_7_eq, comparator_8_eq, comparator_11_eq, comparator_12_eq, comparator_16_eq);
  D_Flip_Flop d_ff_29 (
    .clk(Clock_out), .D(priority_encoder_1_out[0]), .Q(d_ff_29_q), .en(Mode));  // open: Qn, preset, reset
  D_Flip_Flop d_ff_30 (.clk(Clock_out), .D(d_ff_29_q), .Q(d_ff_30_q), .en(Mode));  // open: Qn, preset, reset
  D_Flip_Flop d_ff_31 (.clk(Clock_out), .D(d_ff_30_q), .Q(d_ff_31_q), .en(Mode));  // open: Qn, preset, reset
  D_Flip_Flop d_ff_32 (.clk(Clock_out), .D(d_ff_31_q), .Q(d_ff_32_q), .en(Mode));  // open: Qn, preset, reset
  Display2_Decoder D2_Decoder (
    .X(and_1_out), .a(D2_Decoder_a), .b(D2_Decoder_b), .c(D2_Decoder_c), .d(D2_Decoder_d), .e(D2_Decoder_e),
    .f(D2_Decoder_f), .g(D2_Decoder_g));

  // Notes on the sheet:
  //   Mode 0 = Store Pattern
  //   Mode 1 = Check Pattern
  //   Display1
  //   Display2
  //   O = Match
  //   N = Not Match
endmodule

module Display2_Decoder (
  input  X,
  output a,
  output b,
  output c,
  output d,
  output e,
  output f,
  output g
);

  wire not_1_out;

  not not_1 (not_1_out, X);
  or or_1 (a, X, not_1_out);
  not not_2 (g, a);

  assign b = a;
  assign c = a;
  assign d = X;
  assign e = a;
  assign f = a;
endmodule

module Display1_Decoder (
  input  D,
  input  C,
  input  B,
  input  A,
  output a_2,
  output b_2,
  output c_2,
  output d_2,
  output e,
  output f,
  output g
);

  wire and_1_out, and_2_out, and_3_out, and_4_out, and_5_out, and_6_out, and_7_out, and_8_out, and_10_out,
       and_11_out, not_1_out, not_2_out, not_3_out, or_2_out, or_3_out, or_4_out;

  not not_1 (not_1_out, C);
  not not_2 (not_2_out, B);
  not not_3 (not_3_out, A);
  and and_1 (and_1_out, C, A);
  and and_2 (and_2_out, not_1_out, not_3_out);
  and and_3 (and_3_out, not_2_out, not_3_out);
  and and_4 (and_4_out, B, A);
  or or_1 (c_2, not_2_out, A, C);
  or or_2 (or_2_out, B, not_1_out);
  and and_5 (and_5_out, C, not_2_out, A);
  and and_6 (and_6_out, not_1_out, B);
  or or_3 (or_3_out, not_3_out, C);
  and and_7 (and_7_out, C, not_3_out);
  or or_4 (or_4_out, not_3_out, not_2_out);
  and and_8 (and_8_out, B, not_1_out);
  or or_5 (a_2, and_1_out, and_2_out, B, D);
  or or_6 (b_2, and_3_out, and_4_out, not_1_out);
  and and_9 (e, not_3_out, or_2_out);
  and and_10 (and_10_out, not_2_out, or_3_out);
  and and_11 (and_11_out, or_4_out, C);
  or or_7 (g, and_11_out, and_8_out, D);
  or or_8 (d_2, e, and_5_out, and_6_out, D);
  or or_9 (f, and_10_out, and_7_out, D);
endmodule
