// Logisim project 5 Digit Lock.circ as structural Verilog: 3 circuits, main circuit main
module main (
  input  Mode,
  input  _1,
  input  _2,
  input  _3,
  input  Edit
);

  wire _0_out, _1_out, _2_out, _3_out, _4_out, _5_out, _6_out, _7_out, _8_out, _9_out, and_1_out, and_2_out,
       and_3_out, and_4_out, and_5_out, and_6_out, and_7_out, and_8_out, and_9_out, Clock_out,
       comparator_1_eq, comparator_2_eq, comparator_3_eq, comparator_4_eq, comparator_5_eq, comparator_6_eq,
       comparator_7_eq, comparator_8_eq, comparator_9_eq, comparator_10_eq, comparator_11_eq,
       comparator_12_eq, comparator_13_eq, comparator_14_eq, comparator_15_eq, comparator_16_eq,
       comparator_17_eq, comparator_18_eq, comparator_19_eq, comparator_20_eq, comparator_21_eq,
       comparator_22_eq, comparator_23_eq, comparator_24_eq, comparator_25_eq, comparator_26_eq,
       comparator_27_eq, comparator_28_eq, comparator_29_eq, comparator_30_eq, comparator_31_eq,
       comparator_32_eq, comparator_33_eq, comparator_34_eq, comparator_35_eq, comparator_36_eq,
       comparator_37_eq, comparator_38_eq, comparator_39_eq, comparator_40_eq, comparator_41_eq,
       comparator_42_eq, comparator_43_eq, comparator_44_eq, comparator_45_eq, comparator_46_eq,
       comparator_47_eq, comparator_48_eq, comparator_49_eq, comparator_50_eq, comparator_51_eq,
       comparator_52_eq, comparator_53_eq, comparator_54_eq, comparator_55_eq, comparator_56_eq,
       comparator_57_eq, comparator_58_eq, comparator_59_eq, comparator_60_eq, D1_Decoder_2_a_2,
       D1_Decoder_2_b_2, D1_Decoder_2_c_2, D1_Decoder_2_d_2, D1_Decoder_2_e, D1_Decoder_2_f, D1_Decoder_2_g,
       D1_Decoder_3_a_2, D1_Decoder_3_b_2, D1_Decoder_3_c_2, D1_Decoder_3_d_2, D1_Decoder_3_e,
       D1_Decoder_3_f, D1_Decoder_3_g, D1_Decoder_4_a_2, D1_Decoder_4_b_2, D1_Decoder_4_c_2,
       D1_Decoder_4_d_2, D1_Decoder_4_e, D1_Decoder_4_f, D1_Decoder_4_g, D1_Decoder_a_2, D1_Decoder_b_2,
       D1_Decoder_c_2, D1_Decoder_d_2, D1_Decoder_e, D1_Decoder_f, D1_Decoder_g, D2_Decoder_a, D2_Decoder_b,
       D2_Decoder_c, D2_Decoder_d, D2_Decoder_e, D2_Decoder_f, D2_Decoder_g, d_ff_1_q, d_ff_2_q, d_ff_3_q,
       d_ff_4_q, d_ff_5_q, d_ff_6_q, d_ff_7_q, d_ff_8_q, d_ff_9_q, d_ff_10_q, d_ff_11_q, d_ff_12_q,
       d_ff_13_q, d_ff_14_q, d_ff_15_q, d_ff_16_q, d_ff_17_q, d_ff_18_q, d_ff_19_q, d_ff_20_q, d_ff_21_q,
       d_ff_22_q, d_ff_23_q, d_ff_24_q, d_ff_25_q, d_ff_26_q, d_ff_27_q, d_ff_28_q, d_ff_29_q, d_ff_30_q,
       d_ff_31_q, d_ff_32_q, d_ff_33_q, d_ff_34_q, d_ff_35_q, d_ff_36_q, d_ff_37_q, d_ff_38_q, d_ff_39_q,
       d_ff_40_q, d_ff_41_q, d_ff_42_q, d_ff_43_q, d_ff_44_q, d_ff_45_q, d_ff_46_q, d_ff_47_q, d_ff_48_q,
       d_ff_49_q, d_ff_50_q, d_ff_51_q, d_ff_52_q, d_ff_53_q, d_ff_54_q, d_ff_55_q, d_ff_56_q, d_ff_57_q,
       d_ff_58_q, d_ff_59_q, d_ff_60_q, d_ff_61_q, d_ff_62_q, d_ff_63_q, d_ff_64_q, d_ff_65_q, d_ff_66_q,
       d_ff_67_q, d_ff_68_q, d_ff_69_q, d_ff_70_q, d_ff_71_q, d_ff_72_q, d_ff_73_q, d_ff_74_q, d_ff_75_q,
       d_ff_76_q, d_ff_77_q, d_ff_78_q, d_ff_79_q, d_ff_80_q, Delete_out, display1_decoder_1_a_2,
       display1_decoder_1_b_2, display1_decoder_1_c_2, display1_decoder_1_d_2, display1_decoder_1_e,
       display1_decoder_1_f, display1_decoder_1_g, multiplexer_1_out, multiplexer_2_out, multiplexer_3_out,
       multiplexer_4_out, multiplexer_5_out, multiplexer_6_out, multiplexer_7_out, multiplexer_8_out,
       multiplexer_9_out, multiplexer_10_out, multiplexer_11_out, multiplexer_12_out, multiplexer_13_out,
       multiplexer_14_out, multiplexer_15_out, multiplexer_16_out, multiplexer_17_out, multiplexer_18_out,
       multiplexer_19_out, multiplexer_20_out, multiplexer_21_out, multiplexer_22_out, multiplexer_23_out,
       multiplexer_24_out, multiplexer_25_out, multiplexer_26_out, multiplexer_27_out, multiplexer_28_out,
       multiplexer_29_out, multiplexer_30_out, multiplexer_31_out, multiplexer_32_out, multiplexer_33_out,
       multiplexer_34_out, multiplexer_35_out, multiplexer_36_out, multiplexer_37_out, multiplexer_38_out,
       multiplexer_39_out, multiplexer_40_out, multiplexer_41_out, multiplexer_42_out, multiplexer_43_out,
       multiplexer_44_out, multiplexer_45_out, multiplexer_46_out, multiplexer_47_out, multiplexer_48_out,
       multiplexer_49_out, multiplexer_50_out, multiplexer_51_out, multiplexer_52_out, multiplexer_53_out,
       multiplexer_54_out, multiplexer_55_out, multiplexer_56_out, multiplexer_57_out, multiplexer_58_out,
       multiplexer_59_out, multiplexer_60_out, multiplexer_61_out, multiplexer_62_out, multiplexer_63_out,
       multiplexer_64_out, multiplexer_65_out, multiplexer_66_out, multiplexer_67_out, multiplexer_68_out,
       multiplexer_69_out, multiplexer_70_out, multiplexer_71_out, multiplexer_72_out, multiplexer_73_out,
       multiplexer_74_out, multiplexer_75_out, multiplexer_76_out, multiplexer_77_out, multiplexer_78_out,
       multiplexer_79_out, multiplexer_80_out, multiplexer_81_out, multiplexer_82_out, multiplexer_83_out,
       multiplexer_84_out, multiplexer_85_out, multiplexer_86_out, multiplexer_87_out, multiplexer_88_out,
       multiplexer_89_out, multiplexer_90_out, multiplexer_91_out, multiplexer_92_out, multiplexer_93_out,
       multiplexer_94_out, multiplexer_95_out, multiplexer_96_out, multiplexer_97_out, multiplexer_98_out,
       multiplexer_99_out, multiplexer_100_out, not_1_out, not_2_out, or_1_out, or_2_out,
       priority_encoder_1_gs;
  wire [1:0] priority_encoder_2_out;
  wire [3:0] priority_encoder_1_out;

  Button _0 (.out(_0_out));
  Button u__1 (.out(_1_out));
  Button u__2 (.out(_2_out));
  Button u__3 (.out(_3_out));
  Button _4 (.out(_4_out));
  Button _5 (.out(_5_out));
  Button _6 (.out(_6_out));
  Button _7 (.out(_7_out));
  Button _8 (.out(_8_out));
  Button _9 (.out(_9_out));
  Button Delete (.out(Delete_out));
  Clock Clock (.out(Clock_out));
  not not_1 (not_1_out, Delete_out);
  Priority_Encoder #(.select(4)) priority_encoder_1 (
    .in0(_0_out), .in1(_1_out), .in2(_2_out), .in3(_3_out), .in4(_4_out), .in5(_5_out), .in6(_6_out),
    .in7(_7_out), .in8(_8_out), .in9(_9_out), .out(priority_encoder_1_out), .gs(priority_encoder_1_gs),
    .en_in(or_1_out));  // open: in10, in11, in12, in13, in14, in15, en_out
  and and_1 (and_1_out, _1, not_2_out);
  and and_2 (and_2_out, _2, not_2_out);
  and and_3 (and_3_out, and_2_out, Delete_out);
  and and_4 (and_4_out, and_1_out, Delete_out);
  Priority_Encoder #(.select(2)) priority_encoder_2 (
    .in0(Mode), .in1(and_1_out), .in2(and_2_out), .in3(and_5_out), .out(priority_encoder_2_out),
    .en_in(not_1_out));  // open: gs, en_out
  _7_Segment_Display u_7_segment_display_1 (
    .g(D2_Decoder_g), .f(D2_Decoder_f), .a(D2_Decoder_a), .b(D2_Decoder_b), .e(D2_Decoder_e),
    .d(D2_Decoder_d), .c(D2_Decoder_c));  // open: dp
  not not_2 (not_2_out, Mode);
  and and_5 (and_5_out, _3, not_2_out);
  and and_6 (and_6_out, and_5_out, Delete_out);
  or or_1 (or_1_out, Mode, Edit);
  _7_Segment_Display u_7_segment_display_2 (
    .g(D1_Decoder_g), .f(D1_Decoder_f), .a(D1_Decoder_a_2), .b(D1_Decoder_b_2), .e(D1_Decoder_e),
    .d(D1_Decoder_d_2), .c(D1_Decoder_c_2));  // open: dp
  D_Flip_Flop d_ff_1 (
    .clk(Clock_out), .D(multiplexer_6_out), .Q(d_ff_1_q), .en(and_2_out), .reset(and_3_out));  // open: Qn, preset
  D_Flip_Flop d_ff_2 (
    .clk(Clock_out), .D(multiplexer_7_out), .Q(d_ff_2_q), .en(and_2_out), .reset(and_3_out));  // open: Qn, preset
  D_Flip_Flop d_ff_3 (
    .clk(Clock_out), .D(multiplexer_8_out), .Q(d_ff_3_q), .en(and_2_out), .reset(and_3_out));  // open: Qn, preset
  D_Flip_Flop d_ff_4 (
    .clk(Clock_out), .D(multiplexer_9_out), .Q(d_ff_4_q), .en(and_2_out), .reset(and_3_out));  // open: Qn, preset
  D_Flip_Flop d_ff_5 (
    .clk(Clock_out), .D(multiplexer_10_out), .Q(d_ff_5_q), .en(and_2_out), .reset(and_3_out));  // open: Qn, preset
  Display2_Decoder D2_Decoder (
    .X(or_2_out), .a(D2_Decoder_a), .b(D2_Decoder_b), .c(D2_Decoder_c), .d(D2_Decoder_d), .e(D2_Decoder_e),
    .f(D2_Decoder_f), .g(D2_Decoder_g));
  _7_Segment_Display u_7_segment_display_3 (
    .g(D1_Decoder_3_g), .f(D1_Decoder_3_f), .a(D1_Decoder_3_a_2), .b(D1_Decoder_3_b_2), .e(D1_Decoder_3_e),
    .d(D1_Decoder_3_d_2), .c(D1_Decoder_3_c_2));  // open: dp
  _7_Segment_Display u_7_segment_display_4 (
    .g(D1_Decoder_2_g), .f(D1_Decoder_2_f), .a(D1_Decoder_2_a_2), .b(D1_Decoder_2_b_2), .e(D1_Decoder_2_e),
    .d(D1_Decoder_2_d_2), .c(D1_Decoder_2_c_2));  // open: dp
  D_Flip_Flop d_ff_6 (.clk(Clock_out), .D(multiplexer_1_out), .Q(d_ff_6_q), .en(Mode));  // open: Qn, preset, reset
  Multiplexer multiplexer_1 (
    .in0(d_ff_6_q), .in1(priority_encoder_1_out[3]), .out(multiplexer_1_out), .sel(priority_encoder_1_gs),
    .en(Mode));
  D_Flip_Flop d_ff_7 (.clk(Clock_out), .D(multiplexer_2_out), .Q(d_ff_7_q), .en(Mode));  // open: Qn, preset, reset
  Multiplexer multiplexer_2 (
    .in0(d_ff_7_q), .in1(d_ff_6_q), .out(multiplexer_2_out), .sel(priority_encoder_1_gs), .en(Mode));
  D_Flip_Flop d_ff_8 (.clk(Clock_out), .D(multiplexer_3_out), .Q(d_ff_8_q), .en(Mode));  // open: Qn, preset, reset
  Multiplexer multiplexer_3 (
    .in0(d_ff_8_q), .in1(d_ff_7_q), .out(multiplexer_3_out), .sel(priority_encoder_1_gs), .en(Mode));
  D_Flip_Flop d_ff_9 (.clk(Clock_out), .D(multiplexer_4_out), .Q(d_ff_9_q), .en(Mode));  // open: Qn, preset, reset
  Multiplexer multiplexer_4 (
    .in0(d_ff_9_q), .in1(d_ff_8_q), .out(multiplexer_4_out), .sel(priority_encoder_1_gs), .en(Mode));
  D_Flip_Flop d_ff_10 (.clk(Clock_out), .D(multiplexer_5_out), .Q(d_ff_10_q), .en(Mode));  // open: Qn, preset, reset
  Multiplexer multiplexer_5 (
    .in0(d_ff_10_q), .in1(d_ff_9_q), .out(multiplexer_5_out), .sel(priority_encoder_1_gs), .en(Mode));
  Multiplexer multiplexer_6 (
    .in0(d_ff_1_q), .in1(priority_encoder_1_out[3]), .out(multiplexer_6_out), .sel(priority_encoder_1_gs),
    .en(and_2_out));
  Multiplexer multiplexer_7 (
    .in0(d_ff_2_q), .in1(d_ff_1_q), .out(multiplexer_7_out), .sel(priority_encoder_1_gs), .en(and_2_out));
  Multiplexer multiplexer_8 (
    .in0(d_ff_3_q), .in1(d_ff_2_q), .out(multiplexer_8_out), .sel(priority_encoder_1_gs), .en(and_2_out));
  Multiplexer multiplexer_9 (
    .in0(d_ff_4_q), .in1(d_ff_3_q), .out(multiplexer_9_out), .sel(priority_encoder_1_gs), .en(and_2_out));
  Multiplexer multiplexer_10 (
    .in0(d_ff_5_q), .in1(d_ff_4_q), .out(multiplexer_10_out), .sel(priority_encoder_1_gs), .en(and_2_out));
  _7_Segment_Display u_7_segment_display_5 (
    .g(D1_Decoder_4_g), .f(D1_Decoder_4_f), .a(D1_Decoder_4_a_2), .b(D1_Decoder_4_b_2), .e(D1_Decoder_4_e),
    .d(D1_Decoder_4_d_2), .c(D1_Decoder_4_c_2));  // open: dp
  _7_Segment_Display u_7_segment_display_6 (
    .g(display1_decoder_1_g), .f(display1_decoder_1_f), .a(display1_decoder_1_a_2),
    .b(display1_decoder_1_b_2), .e(display1_decoder_1_e), .d(display1_decoder_1_d_2),
    .c(display1_decoder_1_c_2));  // open: dp
  D_Flip_Flop d_ff_11 (.clk(Clock_out), .D(multiplexer_16_out), .Q(d_ff_11_q), .en(Mode));  // open: Qn, preset, reset
  D_Flip_Flop d_ff_12 (.clk(Clock_out), .D(multiplexer_17_out), .Q(d_ff_12_q), .en(Mode));  // open: Qn, preset, reset
  D_Flip_Flop d_ff_13 (.clk(Clock_out), .D(multiplexer_18_out), .Q(d_ff_13_q), .en(Mode));  // open: Qn, preset, reset
  D_Flip_Flop d_ff_14 (.clk(Clock_out), .D(multiplexer_19_out), .Q(d_ff_14_q), .en(Mode));  // open: Qn, preset, reset
  D_Flip_Flop d_ff_15 (.clk(Clock_out), .D(multiplexer_20_out), .Q(d_ff_15_q), .en(Mode));  // open: Qn, preset, reset
  D_Flip_Flop d_ff_16 (
    .clk(Clock_out), .D(multiplexer_11_out), .Q(d_ff_16_q), .en(and_2_out), .reset(and_3_out));  // open: Qn, preset
  Multiplexer multiplexer_11 (
    .in0(d_ff_16_q), .in1(priority_encoder_1_out[2]), .out(multiplexer_11_out), .sel(priority_encoder_1_gs),
    .en(and_2_out));
  D_Flip_Flop d_ff_17 (
    .clk(Clock_out), .D(multiplexer_12_out), .Q(d_ff_17_q), .en(and_2_out), .reset(and_3_out));  // open: Qn, preset
  Multiplexer multiplexer_12 (
    .in0(d_ff_17_q), .in1(d_ff_16_q), .out(multiplexer_12_out), .sel(priority_encoder_1_gs), .en(and_2_out));
  D_Flip_Flop d_ff_18 (
    .clk(Clock_out), .D(multiplexer_13_out), .Q(d_ff_18_q), .en(and_2_out), .reset(and_3_out));  // open: Qn, preset
  Multiplexer multiplexer_13 (
    .in0(d_ff_18_q), .in1(d_ff_17_q), .out(multiplexer_13_out), .sel(priority_encoder_1_gs), .en(and_2_out));
  D_Flip_Flop d_ff_19 (
    .clk(Clock_out), .D(multiplexer_14_out), .Q(d_ff_19_q), .en(and_2_out), .reset(and_3_out));  // open: Qn, preset
  Multiplexer multiplexer_14 (
    .in0(d_ff_19_q), .in1(d_ff_18_q), .out(multiplexer_14_out), .sel(priority_encoder_1_gs), .en(and_2_out));
  D_Flip_Flop d_ff_20 (
    .clk(Clock_out), .D(multiplexer_15_out), .Q(d_ff_20_q), .en(and_2_out), .reset(and_3_out));  // open: Qn, preset
  Multiplexer multiplexer_15 (
    .in0(d_ff_20_q), .in1(d_ff_19_q), .out(multiplexer_15_out), .sel(priority_encoder_1_gs), .en(and_2_out));
  Multiplexer multiplexer_16 (
    .in0(d_ff_11_q), .in1(priority_encoder_1_out[2]), .out(multiplexer_16_out), .sel(priority_encoder_1_gs),
    .en(Mode));
  Multiplexer multiplexer_17 (
    .in0(d_ff_12_q), .in1(d_ff_11_q), .out(multiplexer_17_out), .sel(priority_encoder_1_gs), .en(Mode));
  Multiplexer multiplexer_18 (
    .in0(d_ff_13_q), .in1(d_ff_12_q), .out(multiplexer_18_out), .sel(priority_encoder_1_gs), .en(Mode));
  Multiplexer multiplexer_19 (
    .in0(d_ff_14_q), .in1(d_ff_13_q), .out(multiplexer_19_out), .sel(priority_encoder_1_gs), .en(Mode));
  Multiplexer multiplexer_20 (
    .in0(d_ff_15_q), .in1(d_ff_14_q), .out(multiplexer_20_out), .sel(priority_encoder_1_gs), .en(Mode));
  D_Flip_Flop d_ff_21 (.clk(Clock_out), .D(multiplexer_21_out), .Q(d_ff_21_q), .en(Mode));  // open: Qn, preset, reset
  D_Flip_Flop d_ff_22 (.clk(Clock_out), .D(multiplexer_22_out), .Q(d_ff_22_q), .en(Mode));  // open: Qn, preset, reset
  D_Flip_Flop d_ff_23 (.clk(Clock_out), .D(multiplexer_23_out), .Q(d_ff_23_q), .en(Mode));  // open: Qn, preset, reset
  D_Flip_Flop d_ff_24 (.clk(Clock_out), .D(multiplexer_24_out), .Q(d_ff_24_q), .en(Mode));  // open: Qn, preset, reset
  D_Flip_Flop d_ff_25 (.clk(Clock_out), .D(multiplexer_25_out), .Q(d_ff_25_q), .en(Mode));  // open: Qn, preset, reset
  Comparator #(.width(1)) comparator_1 (.a(d_ff_6_q), .b(d_ff_41_q), .eq(comparator_1_eq));  // open: gt, lt
  Comparator #(.width(1)) comparator_2 (.a(d_ff_7_q), .b(d_ff_42_q), .eq(comparator_2_eq));  // open: gt, lt
  Comparator #(.width(1)) comparator_3 (.a(d_ff_8_q), .b(d_ff_43_q), .eq(comparator_3_eq));  // open: gt, lt
  Comparator #(.width(1)) comparator_4 (.a(d_ff_9_q), .b(d_ff_44_q), .eq(comparator_4_eq));  // open: gt, lt
  Comparator #(.width(1)) comparator_5 (.a(d_ff_10_q), .b(d_ff_45_q), .eq(comparator_5_eq));  // open: gt, lt
  D_Flip_Flop d_ff_26 (
    .clk(Clock_out), .D(multiplexer_26_out), .Q(d_ff_26_q), .en(and_2_out), .reset(and_3_out));  // open: Qn, preset
  D_Flip_Flop d_ff_27 (
    .clk(Clock_out), .D(multiplexer_27_out), .Q(d_ff_27_q), .en(and_2_out), .reset(and_3_out));  // open: Qn, preset
  D_Flip_Flop d_ff_28 (
    .clk(Clock_out), .D(multiplexer_28_out), .Q(d_ff_28_q), .en(and_2_out), .reset(and_3_out));  // open: Qn, preset
  D_Flip_Flop d_ff_29 (
    .clk(Clock_out), .D(multiplexer_29_out), .Q(d_ff_29_q), .en(and_2_out), .reset(and_3_out));  // open: Qn, preset
  D_Flip_Flop d_ff_30 (
    .clk(Clock_out), .D(multiplexer_30_out), .Q(d_ff_30_q), .en(and_2_out), .reset(and_3_out));  // open: Qn, preset
  Comparator #(.width(1)) comparator_6 (.a(d_ff_1_q), .b(d_ff_6_q), .eq(comparator_6_eq));  // open: gt, lt
  Comparator #(.width(1)) comparator_7 (.a(d_ff_2_q), .b(d_ff_7_q), .eq(comparator_7_eq));  // open: gt, lt
  Comparator #(.width(1)) comparator_8 (.a(d_ff_3_q), .b(d_ff_8_q), .eq(comparator_8_eq));  // open: gt, lt
  Comparator #(.width(1)) comparator_9 (.a(d_ff_4_q), .b(d_ff_9_q), .eq(comparator_9_eq));  // open: gt, lt
  Comparator #(.width(1)) comparator_10 (.a(d_ff_5_q), .b(d_ff_10_q), .eq(comparator_10_eq));  // open: gt, lt
  Comparator #(.width(1)) comparator_11 (.a(d_ff_46_q), .b(d_ff_6_q), .eq(comparator_11_eq));  // open: gt, lt
  Comparator #(.width(1)) comparator_12 (.a(d_ff_47_q), .b(d_ff_7_q), .eq(comparator_12_eq));  // open: gt, lt
  Comparator #(.width(1)) comparator_13 (.a(d_ff_48_q), .b(d_ff_8_q), .eq(comparator_13_eq));  // open: gt, lt
  Comparator #(.width(1)) comparator_14 (.a(d_ff_49_q), .b(d_ff_9_q), .eq(comparator_14_eq));  // open: gt, lt
  Comparator #(.width(1)) comparator_15 (.a(d_ff_50_q), .b(d_ff_10_q), .eq(comparator_15_eq));  // open: gt, lt
  Multiplexer multiplexer_21 (
    .in0(d_ff_21_q), .in1(priority_encoder_1_out[1]), .out(multiplexer_21_out), .sel(priority_encoder_1_gs),
    .en(Mode));
  Multiplexer multiplexer_22 (
    .in0(d_ff_22_q), .in1(d_ff_21_q), .out(multiplexer_22_out), .sel(priority_encoder_1_gs), .en(Mode));
  Multiplexer multiplexer_23 (
    .in0(d_ff_23_q), .in1(d_ff_22_q), .out(multiplexer_23_out), .sel(priority_encoder_1_gs), .en(Mode));
  Multiplexer multiplexer_24 (
    .in0(d_ff_24_q), .in1(d_ff_23_q), .out(multiplexer_24_out), .sel(priority_encoder_1_gs), .en(Mode));
  Multiplexer multiplexer_25 (
    .in0(d_ff_25_q), .in1(d_ff_24_q), .out(multiplexer_25_out), .sel(priority_encoder_1_gs), .en(Mode));
  Multiplexer multiplexer_26 (
    .in0(d_ff_26_q), .in1(priority_encoder_1_out[1]), .out(multiplexer_26_out), .sel(priority_encoder_1_gs),
    .en(and_2_out));
  Multiplexer multiplexer_27 (
    .in0(d_ff_27_q), .in1(d_ff_26_q), .out(multiplexer_27_out), .sel(priority_encoder_1_gs), .en(and_2_out));
  Multiplexer multiplexer_28 (
    .in0(d_ff_28_q), .in1(d_ff_27_q), .out(multiplexer_28_out), .sel(priority_encoder_1_gs), .en(and_2_out));
  Multiplexer multiplexer_29 (
    .in0(d_ff_29_q), .in1(d_ff_28_q), .out(multiplexer_29_out), .sel(priority_encoder_1_gs), .en(and_2_out));
  Multiplexer multiplexer_30 (
    .in0(d_ff_30_q), .in1(d_ff_29_q), .out(multiplexer_30_out), .sel(priority_encoder_1_gs), .en(and_2_out));
  Multiplexer #(.select(2)) multiplexer_31 (
    .in0(d_ff_6_q), .in1(d_ff_41_q), .in2(d_ff_1_q), .in3(d_ff_46_q), .out(multiplexer_31_out),
    .sel(priority_encoder_2_out), .en(not_1_out));
  Multiplexer #(.select(2)) multiplexer_32 (
    .in0(d_ff_7_q), .in1(d_ff_42_q), .in2(d_ff_2_q), .in3(d_ff_47_q), .out(multiplexer_32_out),
    .sel(priority_encoder_2_out), .en(not_1_out));
  Multiplexer #(.select(2)) multiplexer_33 (
    .in0(d_ff_8_q), .in1(d_ff_43_q), .in2(d_ff_3_q), .in3(d_ff_48_q), .out(multiplexer_33_out),
    .sel(priority_encoder_2_out), .en(not_1_out));
  Multiplexer #(.select(2)) multiplexer_34 (
    .in0(d_ff_9_q), .in1(d_ff_44_q), .in2(d_ff_4_q), .in3(d_ff_49_q), .out(multiplexer_34_out),
    .sel(priority_encoder_2_out), .en(not_1_out));
  Multiplexer #(.select(2)) multiplexer_35 (
    .in0(d_ff_10_q), .in1(d_ff_45_q), .in2(d_ff_5_q), .in3(d_ff_50_q), .out(multiplexer_35_out),
    .sel(priority_encoder_2_out), .en(not_1_out));
  D_Flip_Flop d_ff_31 (.clk(Clock_out), .D(multiplexer_41_out), .Q(d_ff_31_q), .en(Mode));  // open: Qn, preset, reset
  D_Flip_Flop d_ff_32 (.clk(Clock_out), .D(multiplexer_42_out), .Q(d_ff_32_q), .en(Mode));  // open: Qn, preset, reset
  D_Flip_Flop d_ff_33 (.clk(Clock_out), .D(multiplexer_43_out), .Q(d_ff_33_q), .en(Mode));  // open: Qn, preset, reset
  D_Flip_Flop d_ff_34 (.clk(Clock_out), .D(multiplexer_44_out), .Q(d_ff_34_q), .en(Mode));  // open: Qn, preset, reset
  D_Flip_Flop d_ff_35 (.clk(Clock_out), .D(multiplexer_45_out), .Q(d_ff_35_q), .en(Mode));  // open: Qn, preset, reset
  Comparator #(.width(1)) comparator_16 (.a(d_ff_11_q), .b(d_ff_51_q), .eq(comparator_16_eq));  // open: gt, lt
  Comparator #(.width(1)) comparator_17 (.a(d_ff_12_q), .b(d_ff_52_q), .eq(comparator_17_eq));  // open: gt, lt
  Comparator #(.width(1)) comparator_18 (.a(d_ff_13_q), .b(d_ff_53_q), .eq(comparator_18_eq));  // open: gt, lt
  Comparator #(.width(1)) comparator_19 (.a(d_ff_14_q), .b(d_ff_54_q), .eq(comparator_19_eq));  // open: gt, lt
  Comparator #(.width(1)) comparator_20 (.a(d_ff_15_q), .b(d_ff_55_q), .eq(comparator_20_eq));  // open: gt, lt
  D_Flip_Flop d_ff_36 (
    .clk(Clock_out), .D(multiplexer_36_out), .Q(d_ff_36_q), .en(and_2_out), .reset(and_3_out));  // open: Qn, preset
  Multiplexer multiplexer_36 (
    .in0(d_ff_36_q), .in1(priority_encoder_1_out[0]), .out(multiplexer_36_out), .sel(priority_encoder_1_gs),
    .en(and_2_out));
  D_Flip_Flop d_ff_37 (
    .clk(Clock_out), .D(multiplexer_37_out), .Q(d_ff_37_q), .en(and_2_out), .reset(and_3_out));  // open: Qn, preset
  Multiplexer multiplexer_37 (
    .in0(d_ff_37_q), .in1(d_ff_36_q), .out(multiplexer_37_out), .sel(priority_encoder_1_gs), .en(and_2_out));
  D_Flip_Flop d_ff_38 (
    .clk(Clock_out), .D(multiplexer_38_out), .Q(d_ff_38_q), .en(and_2_out), .reset(and_3_out));  // open: Qn, preset
  Multiplexer multiplexer_38 (
    .in0(d_ff_38_q), .in1(d_ff_37_q), .out(multiplexer_38_out), .sel(priority_encoder_1_gs), .en(and_2_out));
  D_Flip_Flop d_ff_39 (
    .clk(Clock_out), .D(multiplexer_39_out), .Q(d_ff_39_q), .en(and_2_out), .reset(and_3_out));  // open: Qn, preset
  Multiplexer multiplexer_39 (
    .in0(d_ff_39_q), .in1(d_ff_38_q), .out(multiplexer_39_out), .sel(priority_encoder_1_gs), .en(and_2_out));
  D_Flip_Flop d_ff_40 (
    .clk(Clock_out), .D(multiplexer_40_out), .Q(d_ff_40_q), .en(and_2_out), .reset(and_3_out));  // open: Qn, preset
  Multiplexer multiplexer_40 (
    .in0(d_ff_40_q), .in1(d_ff_39_q), .out(multiplexer_40_out), .sel(priority_encoder_1_gs), .en(and_2_out));
  Comparator #(.width(1)) comparator_21 (.a(d_ff_16_q), .b(d_ff_11_q), .eq(comparator_21_eq));  // open: gt, lt
  Comparator #(.width(1)) comparator_22 (.a(d_ff_17_q), .b(d_ff_12_q), .eq(comparator_22_eq));  // open: gt, lt
  Comparator #(.width(1)) comparator_23 (.a(d_ff_18_q), .b(d_ff_13_q), .eq(comparator_23_eq));  // open: gt, lt
  Comparator #(.width(1)) comparator_24 (.a(d_ff_19_q), .b(d_ff_14_q), .eq(comparator_24_eq));  // open: gt, lt
  Comparator #(.width(1)) comparator_25 (.a(d_ff_20_q), .b(d_ff_15_q), .eq(comparator_25_eq));  // open: gt, lt
  Comparator #(.width(1)) comparator_26 (.a(d_ff_56_q), .b(d_ff_11_q), .eq(comparator_26_eq));  // open: gt, lt
  Comparator #(.width(1)) comparator_27 (.a(d_ff_57_q), .b(d_ff_12_q), .eq(comparator_27_eq));  // open: gt, lt
  Comparator #(.width(1)) comparator_28 (.a(d_ff_58_q), .b(d_ff_13_q), .eq(comparator_28_eq));  // open: gt, lt
  Comparator #(.width(1)) comparator_29 (.a(d_ff_59_q), .b(d_ff_14_q), .eq(comparator_29_eq));  // open: gt, lt
  Comparator #(.width(1)) comparator_30 (.a(d_ff_60_q), .b(d_ff_15_q), .eq(comparator_30_eq));  // open: gt, lt
  Multiplexer multiplexer_41 (
    .in0(d_ff_31_q), .in1(priority_encoder_1_out[0]), .out(multiplexer_41_out), .sel(priority_encoder_1_gs),
    .en(Mode));
  Multiplexer multiplexer_42 (
    .in0(d_ff_32_q), .in1(d_ff_31_q), .out(multiplexer_42_out), .sel(priority_encoder_1_gs), .en(Mode));
  Multiplexer multiplexer_43 (
    .in0(d_ff_33_q), .in1(d_ff_32_q), .out(multiplexer_43_out), .sel(priority_encoder_1_gs), .en(Mode));
  Multiplexer multiplexer_44 (
    .in0(d_ff_34_q), .in1(d_ff_33_q), .out(multiplexer_44_out), .sel(priority_encoder_1_gs), .en(Mode));
  Multiplexer multiplexer_45 (
    .in0(d_ff_35_q), .in1(d_ff_34_q), .out(multiplexer_45_out), .sel(priority_encoder_1_gs), .en(Mode));
  Multiplexer #(.select(2)) multiplexer_46 (
    .in0(d_ff_11_q), .in1(d_ff_51_q), .in2(d_ff_16_q), .in3(d_ff_56_q), .out(multiplexer_46_out),
    .sel(priority_encoder_2_out), .en(not_1_out));
  Multiplexer #(.select(2)) multiplexer_47 (
    .in0(d_ff_12_q), .in1(d_ff_52_q), .in2(d_ff_17_q), .in3(d_ff_57_q), .out(multiplexer_47_out),
    .sel(priority_encoder_2_out), .en(not_1_out));
  Multiplexer #(.select(2)) multiplexer_48 (
    .in0(d_ff_13_q), .in1(d_ff_53_q), .in2(d_ff_18_q), .in3(d_ff_58_q), .out(multiplexer_48_out),
    .sel(priority_encoder_2_out), .en(not_1_out));
  Multiplexer #(.select(2)) multiplexer_49 (
    .in0(d_ff_14_q), .in1(d_ff_54_q), .in2(d_ff_19_q), .in3(d_ff_59_q), .out(multiplexer_49_out),
    .sel(priority_encoder_2_out), .en(not_1_out));
  Multiplexer #(.select(2)) multiplexer_50 (
    .in0(d_ff_15_q), .in1(d_ff_55_q), .in2(d_ff_20_q), .in3(d_ff_60_q), .out(multiplexer_50_out),
    .sel(priority_encoder_2_out), .en(not_1_out));
  Display1_Decoder D1_Decoder (
    .D(multiplexer_31_out), .C(multiplexer_46_out), .B(multiplexer_62_out), .A(multiplexer_86_out),
    .a_2(D1_Decoder_a_2), .b_2(D1_Decoder_b_2), .c_2(D1_Decoder_c_2), .d_2(D1_Decoder_d_2), .e(D1_Decoder_e),
    .f(D1_Decoder_f), .g(D1_Decoder_g));
  D_Flip_Flop d_ff_41 (
    .clk(Clock_out), .D(multiplexer_51_out), .Q(d_ff_41_q), .en(and_1_out), .reset(and_4_out));  // open: Qn, preset
  D_Flip_Flop d_ff_42 (
    .clk(Clock_out), .D(multiplexer_52_out), .Q(d_ff_42_q), .en(and_1_out), .reset(and_4_out));  // open: Qn, preset
  D_Flip_Flop d_ff_43 (
    .clk(Clock_out), .D(multiplexer_53_out), .Q(d_ff_43_q), .en(and_1_out), .reset(and_4_out));  // open: Qn, preset
  D_Flip_Flop d_ff_44 (
    .clk(Clock_out), .D(multiplexer_54_out), .Q(d_ff_44_q), .en(and_1_out), .reset(and_4_out));  // open: Qn, preset
  D_Flip_Flop d_ff_45 (
    .clk(Clock_out), .D(multiplexer_55_out), .Q(d_ff_45_q), .en(and_1_out), .reset(and_4_out));  // open: Qn, preset
  Comparator #(.width(1)) comparator_31 (.a(d_ff_21_q), .b(d_ff_61_q), .eq(comparator_31_eq));  // open: gt, lt
  Comparator #(.width(1)) comparator_32 (.a(d_ff_22_q), .b(d_ff_62_q), .eq(comparator_32_eq));  // open: gt, lt
  Comparator #(.width(1)) comparator_33 (.a(d_ff_23_q), .b(d_ff_63_q), .eq(comparator_33_eq));  // open: gt, lt
  Comparator #(.width(1)) comparator_34 (.a(d_ff_24_q), .b(d_ff_64_q), .eq(comparator_34_eq));  // open: gt, lt
  Comparator #(.width(1)) comparator_35 (.a(d_ff_25_q), .b(d_ff_65_q), .eq(comparator_35_eq));  // open: gt, lt
  D_Flip_Flop d_ff_46 (
    .clk(Clock_out), .D(multiplexer_56_out), .Q(d_ff_46_q), .en(and_5_out), .reset(and_6_out));  // open: Qn, preset
  D_Flip_Flop d_ff_47 (
    .clk(Clock_out), .D(multiplexer_57_out), .Q(d_ff_47_q), .en(and_5_out), .reset(and_6_out));  // open: Qn, preset
  D_Flip_Flop d_ff_48 (
    .clk(Clock_out), .D(multiplexer_58_out), .Q(d_ff_48_q), .en(and_5_out), .reset(and_6_out));  // open: Qn, preset
  D_Flip_Flop d_ff_49 (
    .clk(Clock_out), .D(multiplexer_59_out), .Q(d_ff_49_q), .en(and_5_out), .reset(and_6_out));  // open: Qn, preset
  D_Flip_Flop d_ff_50 (
    .clk(Clock_out), .D(multiplexer_60_out), .Q(d_ff_50_q), .en(and_5_out), .reset(and_6_out));  // open: Qn, preset
  Comparator #(.width(1)) comparator_36 (.a(d_ff_26_q), .b(d_ff_21_q), .eq(comparator_36_eq));  // open: gt, lt
  Comparator #(.width(1)) comparator_37 (.a(d_ff_27_q), .b(d_ff_22_q), .eq(comparator_37_eq));  // open: gt, lt
  Comparator #(.width(1)) comparator_38 (.a(d_ff_28_q), .b(d_ff_23_q), .eq(comparator_38_eq));  // open: gt, lt
  Comparator #(.width(1)) comparator_39 (.a(d_ff_29_q), .b(d_ff_24_q), .eq(comparator_39_eq));  // open: gt, lt
  Comparator #(.width(1)) comparator_40 (.a(d_ff_30_q), .b(d_ff_25_q), .eq(comparator_40_eq));  // open: gt, lt
  Comparator #(.width(1)) comparator_41 (.a(d_ff_66_q), .b(d_ff_21_q), .eq(comparator_41_eq));  // open: gt, lt
  Comparator #(.width(1)) comparator_42 (.a(d_ff_67_q), .b(d_ff_22_q), .eq(comparator_42_eq));  // open: gt, lt
  Comparator #(.width(1)) comparator_43 (.a(d_ff_68_q), .b(d_ff_23_q), .eq(comparator_43_eq));  // open: gt, lt
  Comparator #(.width(1)) comparator_44 (.a(d_ff_69_q), .b(d_ff_24_q), .eq(comparator_44_eq));  // open: gt, lt
  Comparator #(.width(1)) comparator_45 (.a(d_ff_70_q), .b(d_ff_25_q), .eq(comparator_45_eq));  // open: gt, lt
  Multiplexer multiplexer_51 (
    .in0(d_ff_41_q), .in1(priority_encoder_1_out[3]), .out(multiplexer_51_out), .sel(priority_encoder_1_gs),
    .en(and_1_out));
  Multiplexer multiplexer_52 (
    .in0(d_ff_42_q), .in1(d_ff_41_q), .out(multiplexer_52_out), .sel(priority_encoder_1_gs), .en(and_1_out));
  Multiplexer multiplexer_53 (
    .in0(d_ff_43_q), .in1(d_ff_42_q), .out(multiplexer_53_out), .sel(priority_encoder_1_gs), .en(and_1_out));
  Multiplexer multiplexer_54 (
    .in0(d_ff_44_q), .in1(d_ff_43_q), .out(multiplexer_54_out), .sel(priority_encoder_1_gs), .en(and_1_out));
  Multiplexer multiplexer_55 (
    .in0(d_ff_45_q), .in1(d_ff_44_q), .out(multiplexer_55_out), .sel(priority_encoder_1_gs), .en(and_1_out));
  Multiplexer multiplexer_56 (
    .in0(d_ff_46_q), .in1(priority_encoder_1_out[3]), .out(multiplexer_56_out), .sel(priority_encoder_1_gs),
    .en(and_5_out));
  Multiplexer multiplexer_57 (
    .in0(d_ff_47_q), .in1(d_ff_46_q), .out(multiplexer_57_out), .sel(priority_encoder_1_gs), .en(and_5_out));
  Multiplexer multiplexer_58 (
    .in0(d_ff_48_q), .in1(d_ff_47_q), .out(multiplexer_58_out), .sel(priority_encoder_1_gs), .en(and_5_out));
  Multiplexer multiplexer_59 (
    .in0(d_ff_49_q), .in1(d_ff_48_q), .out(multiplexer_59_out), .sel(priority_encoder_1_gs), .en(and_5_out));
  Multiplexer multiplexer_60 (
    .in0(d_ff_50_q), .in1(d_ff_49_q), .out(multiplexer_60_out), .sel(priority_encoder_1_gs), .en(and_5_out));
  Display1_Decoder D1_Decoder_2 (
    .D(multiplexer_32_out), .C(multiplexer_47_out), .B(multiplexer_63_out), .A(multiplexer_87_out),
    .a_2(D1_Decoder_2_a_2), .b_2(D1_Decoder_2_b_2), .c_2(D1_Decoder_2_c_2), .d_2(D1_Decoder_2_d_2),
    .e(D1_Decoder_2_e), .f(D1_Decoder_2_f), .g(D1_Decoder_2_g));
  D_Flip_Flop d_ff_51 (
    .clk(Clock_out), .D(multiplexer_67_out), .Q(d_ff_51_q), .en(and_1_out), .reset(and_4_out));  // open: Qn, preset
  D_Flip_Flop d_ff_52 (
    .clk(Clock_out), .D(multiplexer_68_out), .Q(d_ff_52_q), .en(and_1_out), .reset(and_4_out));  // open: Qn, preset
  D_Flip_Flop d_ff_53 (
    .clk(Clock_out), .D(multiplexer_69_out), .Q(d_ff_53_q), .en(and_1_out), .reset(and_4_out));  // open: Qn, preset
  D_Flip_Flop d_ff_54 (
    .clk(Clock_out), .D(multiplexer_70_out), .Q(d_ff_54_q), .en(and_1_out), .reset(and_4_out));  // open: Qn, preset
  D_Flip_Flop d_ff_55 (
    .clk(Clock_out), .D(multiplexer_71_out), .Q(d_ff_55_q), .en(and_1_out), .reset(and_4_out));  // open: Qn, preset
  Comparator #(.width(1)) comparator_46 (.a(d_ff_31_q), .b(d_ff_71_q), .eq(comparator_46_eq));  // open: gt, lt
  Comparator #(.width(1)) comparator_47 (.a(d_ff_32_q), .b(d_ff_72_q), .eq(comparator_47_eq));  // open: gt, lt
  Comparator #(.width(1)) comparator_48 (.a(d_ff_33_q), .b(d_ff_73_q), .eq(comparator_48_eq));  // open: gt, lt
  Comparator #(.width(1)) comparator_49 (.a(d_ff_34_q), .b(d_ff_74_q), .eq(comparator_49_eq));  // open: gt, lt
  Comparator #(.width(1)) comparator_50 (.a(d_ff_35_q), .b(d_ff_75_q), .eq(comparator_50_eq));  // open: gt, lt
  D_Flip_Flop d_ff_56 (
    .clk(Clock_out), .D(multiplexer_72_out), .Q(d_ff_56_q), .en(and_5_out), .reset(and_6_out));  // open: Qn, preset
  D_Flip_Flop d_ff_57 (
    .clk(Clock_out), .D(multiplexer_73_out), .Q(d_ff_57_q), .en(and_5_out), .reset(and_6_out));  // open: Qn, preset
  D_Flip_Flop d_ff_58 (
    .clk(Clock_out), .D(multiplexer_74_out), .Q(d_ff_58_q), .en(and_5_out), .reset(and_6_out));  // open: Qn, preset
  D_Flip_Flop d_ff_59 (
    .clk(Clock_out), .D(multiplexer_61_out), .Q(d_ff_59_q), .en(and_5_out), .reset(and_6_out));  // open: Qn, preset
  Multiplexer multiplexer_61 (
    .in0(d_ff_59_q), .in1(d_ff_58_q), .out(multiplexer_61_out), .sel(priority_encoder_1_gs), .en(and_5_out));
  D_Flip_Flop d_ff_60 (
    .clk(Clock_out), .D(multiplexer_75_out), .Q(d_ff_60_q), .en(and_5_out), .reset(and_6_out));  // open: Qn, preset
  Comparator #(.width(1)) comparator_51 (.a(d_ff_36_q), .b(d_ff_31_q), .eq(comparator_51_eq));  // open: gt, lt
  Comparator #(.width(1)) comparator_52 (.a(d_ff_37_q), .b(d_ff_32_q), .eq(comparator_52_eq));  // open: gt, lt
  Comparator #(.width(1)) comparator_53 (.a(d_ff_38_q), .b(d_ff_33_q), .eq(comparator_53_eq));  // open: gt, lt
  Comparator #(.width(1)) comparator_54 (.a(d_ff_39_q), .b(d_ff_34_q), .eq(comparator_54_eq));  // open: gt, lt
  Comparator #(.width(1)) comparator_55 (.a(d_ff_40_q), .b(d_ff_35_q), .eq(comparator_55_eq));  // open: gt, lt
  Comparator #(.width(1)) comparator_56 (.a(d_ff_76_q), .b(d_ff_31_q), .eq(comparator_56_eq));  // open: gt, lt
  Comparator #(.width(1)) comparator_57 (.a(d_ff_77_q), .b(d_ff_32_q), .eq(comparator_57_eq));  // open: gt, lt
  Comparator #(.width(1)) comparator_58 (.a(d_ff_78_q), .b(d_ff_33_q), .eq(comparator_58_eq));  // open: gt, lt
  Comparator #(.width(1)) comparator_59 (.a(d_ff_79_q), .b(d_ff_34_q), .eq(comparator_59_eq));  // open: gt, lt
  Comparator #(.width(1)) comparator_60 (.a(d_ff_80_q), .b(d_ff_35_q), .eq(comparator_60_eq));  // open: gt, lt
  Multiplexer #(.select(2)) multiplexer_62 (
    .in0(d_ff_21_q), .in1(d_ff_61_q), .in2(d_ff_26_q), .in3(d_ff_66_q), .out(multiplexer_62_out),
    .sel(priority_encoder_2_out), .en(not_1_out));
  Multiplexer #(.select(2)) multiplexer_63 (
    .in0(d_ff_22_q), .in1(d_ff_62_q), .in2(d_ff_27_q), .in3(d_ff_67_q), .out(multiplexer_63_out),
    .sel(priority_encoder_2_out), .en(not_1_out));
  Multiplexer #(.select(2)) multiplexer_64 (
    .in0(d_ff_23_q), .in1(d_ff_63_q), .in2(d_ff_30_q), .in3(d_ff_68_q), .out(multiplexer_64_out),
    .sel(priority_encoder_2_out), .en(not_1_out));
  Multiplexer #(.select(2)) multiplexer_65 (
    .in0(d_ff_24_q), .in1(d_ff_64_q), .in2(d_ff_29_q), .in3(d_ff_69_q), .out(multiplexer_65_out),
    .sel(priority_encoder_2_out), .en(not_1_out));
  Multiplexer #(.select(2)) multiplexer_66 (
    .in0(d_ff_25_q), .in1(d_ff_65_q), .in2(d_ff_30_q), .in3(d_ff_70_q), .out(multiplexer_66_out),
    .sel(priority_encoder_2_out), .en(not_1_out));
  Multiplexer multiplexer_67 (
    .in0(d_ff_51_q), .in1(priority_encoder_1_out[2]), .out(multiplexer_67_out), .sel(priority_encoder_1_gs),
    .en(and_1_out));
  Multiplexer multiplexer_68 (
    .in0(d_ff_52_q), .in1(d_ff_51_q), .out(multiplexer_68_out), .sel(priority_encoder_1_gs), .en(and_1_out));
  Multiplexer multiplexer_69 (
    .in0(d_ff_53_q), .in1(d_ff_52_q), .out(multiplexer_69_out), .sel(priority_encoder_1_gs), .en(and_1_out));
  Multiplexer multiplexer_70 (
    .in0(d_ff_54_q), .in1(d_ff_53_q), .out(multiplexer_70_out), .sel(priority_encoder_1_gs), .en(and_1_out));
  Multiplexer multiplexer_71 (
    .in0(d_ff_55_q), .in1(d_ff_54_q), .out(multiplexer_71_out), .sel(priority_encoder_1_gs), .en(and_1_out));
  Multiplexer multiplexer_72 (
    .in0(d_ff_56_q), .in1(priority_encoder_1_out[2]), .out(multiplexer_72_out), .sel(priority_encoder_1_gs),
    .en(and_5_out));
  Multiplexer multiplexer_73 (
    .in0(d_ff_57_q), .in1(d_ff_56_q), .out(multiplexer_73_out), .sel(priority_encoder_1_gs), .en(and_5_out));
  Multiplexer multiplexer_74 (
    .in0(d_ff_58_q), .in1(d_ff_57_q), .out(multiplexer_74_out), .sel(priority_encoder_1_gs), .en(and_5_out));
  Multiplexer multiplexer_75 (
    .in0(d_ff_60_q), .in1(d_ff_59_q), .out(multiplexer_75_out), .sel(priority_encoder_1_gs), .en(and_5_out));
  Display1_Decoder D1_Decoder_3 (
    .D(multiplexer_33_out), .C(multiplexer_48_out), .B(multiplexer_64_out), .A(multiplexer_88_out),
    .a_2(D1_Decoder_3_a_2), .b_2(D1_Decoder_3_b_2), .c_2(D1_Decoder_3_c_2), .d_2(D1_Decoder_3_d_2),
    .e(D1_Decoder_3_e), .f(D1_Decoder_3_f), .g(D1_Decoder_3_g));
  D_Flip_Flop d_ff_61 (
    .clk(Clock_out), .D(multiplexer_76_out), .Q(d_ff_61_q), .en(and_1_out), .reset(and_4_out));  // open: Qn, preset
  D_Flip_Flop d_ff_62 (
    .clk(Clock_out), .D(multiplexer_77_out), .Q(d_ff_62_q), .en(and_1_out), .reset(and_4_out));  // open: Qn, preset
  D_Flip_Flop d_ff_63 (
    .clk(Clock_out), .D(multiplexer_78_out), .Q(d_ff_63_q), .en(and_1_out), .reset(and_4_out));  // open: Qn, preset
  D_Flip_Flop d_ff_64 (
    .clk(Clock_out), .D(multiplexer_79_out), .Q(d_ff_64_q), .en(and_1_out), .reset(and_4_out));  // open: Qn, preset
  D_Flip_Flop d_ff_65 (
    .clk(Clock_out), .D(multiplexer_80_out), .Q(d_ff_65_q), .en(and_1_out), .reset(and_4_out));  // open: Qn, preset
  D_Flip_Flop d_ff_66 (
    .clk(Clock_out), .D(multiplexer_81_out), .Q(d_ff_66_q), .en(and_5_out), .reset(and_6_out));  // open: Qn, preset
  D_Flip_Flop d_ff_67 (
    .clk(Clock_out), .D(multiplexer_82_out), .Q(d_ff_67_q), .en(and_5_out), .reset(and_6_out));  // open: Qn, preset
  D_Flip_Flop d_ff_68 (
    .clk(Clock_out), .D(multiplexer_83_out), .Q(d_ff_68_q), .en(and_5_out), .reset(and_6_out));  // open: Qn, preset
  D_Flip_Flop d_ff_69 (
    .clk(Clock_out), .D(multiplexer_84_out), .Q(d_ff_69_q), .en(and_5_out), .reset(and_6_out));  // open: Qn, preset
  D_Flip_Flop d_ff_70 (
    .clk(Clock_out), .D(multiplexer_85_out), .Q(d_ff_70_q), .en(and_5_out), .reset(and_6_out));  // open: Qn, preset
  Multiplexer multiplexer_76 (
    .in0(d_ff_61_q), .in1(priority_encoder_1_out[1]), .out(multiplexer_76_out), .sel(priority_encoder_1_gs),
    .en(and_1_out));
  Multiplexer multiplexer_77 (
    .in0(d_ff_62_q), .in1(d_ff_61_q), .out(multiplexer_77_out), .sel(priority_encoder_1_gs), .en(and_1_out));
  Multiplexer multiplexer_78 (
    .in0(d_ff_63_q), .in1(d_ff_62_q), .out(multiplexer_78_out), .sel(priority_encoder_1_gs), .en(and_1_out));
  Multiplexer multiplexer_79 (
    .in0(d_ff_64_q), .in1(d_ff_63_q), .out(multiplexer_79_out), .sel(priority_encoder_1_gs), .en(and_1_out));
  Multiplexer multiplexer_80 (
    .in0(d_ff_65_q), .in1(d_ff_64_q), .out(multiplexer_80_out), .sel(priority_encoder_1_gs), .en(and_1_out));
  Multiplexer multiplexer_81 (
    .in0(d_ff_66_q), .in1(priority_encoder_1_out[1]), .out(multiplexer_81_out), .sel(priority_encoder_1_gs),
    .en(and_5_out));
  Multiplexer multiplexer_82 (
    .in0(d_ff_67_q), .in1(d_ff_66_q), .out(multiplexer_82_out), .sel(priority_encoder_1_gs), .en(and_5_out));
  Multiplexer multiplexer_83 (
    .in0(d_ff_68_q), .in1(d_ff_67_q), .out(multiplexer_83_out), .sel(priority_encoder_1_gs), .en(and_5_out));
  Multiplexer multiplexer_84 (
    .in0(d_ff_69_q), .in1(d_ff_68_q), .out(multiplexer_84_out), .sel(priority_encoder_1_gs), .en(and_5_out));
  Multiplexer multiplexer_85 (
    .in0(d_ff_70_q), .in1(d_ff_69_q), .out(multiplexer_85_out), .sel(priority_encoder_1_gs), .en(and_5_out));
  Multiplexer #(.select(2)) multiplexer_86 (
    .in0(d_ff_31_q), .in1(d_ff_71_q), .in2(d_ff_36_q), .in3(d_ff_76_q), .out(multiplexer_86_out),
    .sel(priority_encoder_2_out), .en(not_1_out));
  Multiplexer #(.select(2)) multiplexer_87 (
    .in0(d_ff_32_q), .in1(d_ff_72_q), .in2(d_ff_37_q), .in3(d_ff_77_q), .out(multiplexer_87_out),
    .sel(priority_encoder_2_out), .en(not_1_out));
  Multiplexer #(.select(2)) multiplexer_88 (
    .in0(d_ff_33_q), .in1(d_ff_73_q), .in2(d_ff_38_q), .in3(d_ff_78_q), .out(multiplexer_88_out),
    .sel(priority_encoder_2_out), .en(not_1_out));
  Multiplexer #(.select(2)) multiplexer_89 (
    .in0(d_ff_34_q), .in1(d_ff_74_q), .in2(d_ff_39_q), .in3(d_ff_79_q), .out(multiplexer_89_out),
    .sel(priority_encoder_2_out), .en(not_1_out));
  Multiplexer #(.select(2)) multiplexer_90 (
    .in0(d_ff_35_q), .in1(d_ff_75_q), .in2(d_ff_40_q), .in3(d_ff_80_q), .out(multiplexer_90_out),
    .sel(priority_encoder_2_out), .en(not_1_out));
  Display1_Decoder D1_Decoder_4 (
    .D(multiplexer_34_out), .C(multiplexer_49_out), .B(multiplexer_65_out), .A(multiplexer_89_out),
    .a_2(D1_Decoder_4_a_2), .b_2(D1_Decoder_4_b_2), .c_2(D1_Decoder_4_c_2), .d_2(D1_Decoder_4_d_2),
    .e(D1_Decoder_4_e), .f(D1_Decoder_4_f), .g(D1_Decoder_4_g));
  D_Flip_Flop d_ff_71 (
    .clk(Clock_out), .D(multiplexer_96_out), .Q(d_ff_71_q), .en(and_1_out), .reset(and_4_out));  // open: Qn, preset
  D_Flip_Flop d_ff_72 (
    .clk(Clock_out), .D(multiplexer_97_out), .Q(d_ff_72_q), .en(and_1_out), .reset(and_4_out));  // open: Qn, preset
  D_Flip_Flop d_ff_73 (
    .clk(Clock_out), .D(multiplexer_98_out), .Q(d_ff_73_q), .en(and_1_out), .reset(and_4_out));  // open: Qn, preset
  D_Flip_Flop d_ff_74 (
    .clk(Clock_out), .D(multiplexer_99_out), .Q(d_ff_74_q), .en(and_1_out), .reset(and_4_out));  // open: Qn, preset
  D_Flip_Flop d_ff_75 (
    .clk(Clock_out), .D(multiplexer_100_out), .Q(d_ff_75_q), .en(and_1_out), .reset(and_4_out));  // open: Qn, preset
  and and_7 (and_7_out, comparator_48_eq, comparator_1_eq, comparator_16_eq, comparator_31_eq, comparator_46_eq, comparator_2_eq, comparator_3_eq, comparator_4_eq, comparator_17_eq, comparator_47_eq, comparator_18_eq, comparator_19_eq, comparator_33_eq, comparator_34_eq, comparator_49_eq, comparator_5_eq, comparator_20_eq, comparator_35_eq, comparator_50_eq);
  D_Flip_Flop d_ff_76 (
    .clk(Clock_out), .D(multiplexer_91_out), .Q(d_ff_76_q), .en(and_5_out), .reset(and_6_out));  // open: Qn, preset
  Multiplexer multiplexer_91 (
    .in0(d_ff_76_q), .in1(priority_encoder_1_out[0]), .out(multiplexer_91_out), .sel(priority_encoder_1_gs),
    .en(and_5_out));
  D_Flip_Flop d_ff_77 (
    .clk(Clock_out), .D(multiplexer_92_out), .Q(d_ff_77_q), .en(and_5_out), .reset(and_6_out));  // open: Qn, preset
  Multiplexer multiplexer_92 (
    .in0(d_ff_77_q), .in1(d_ff_76_q), .out(multiplexer_92_out), .sel(priority_encoder_1_gs), .en(and_5_out));
  D_Flip_Flop d_ff_78 (
    .clk(Clock_out), .D(multiplexer_93_out), .Q(d_ff_78_q), .en(and_5_out), .reset(and_6_out));  // open: Qn, preset
  Multiplexer multiplexer_93 (
    .in0(d_ff_78_q), .in1(d_ff_77_q), .out(multiplexer_93_out), .sel(priority_encoder_1_gs), .en(and_5_out));
  D_Flip_Flop d_ff_79 (
    .clk(Clock_out), .D(multiplexer_94_out), .Q(d_ff_79_q), .en(and_5_out), .reset(and_6_out));  // open: Qn, preset
  Multiplexer multiplexer_94 (
    .in0(d_ff_79_q), .in1(d_ff_78_q), .out(multiplexer_94_out), .sel(priority_encoder_1_gs), .en(and_5_out));
  D_Flip_Flop d_ff_80 (
    .clk(Clock_out), .D(multiplexer_95_out), .Q(d_ff_80_q), .en(and_5_out), .reset(and_6_out));  // open: Qn, preset
  Multiplexer multiplexer_95 (
    .in0(d_ff_80_q), .in1(d_ff_79_q), .out(multiplexer_95_out), .sel(priority_encoder_1_gs), .en(and_5_out));
  and and_8 (and_8_out, comparator_53_eq, comparator_6_eq, comparator_21_eq, comparator_36_eq, comparator_51_eq, comparator_7_eq, comparator_8_eq, comparator_9_eq, comparator_22_eq, comparator_52_eq, comparator_23_eq, comparator_24_eq, comparator_38_eq, comparator_39_eq, comparator_54_eq, comparator_10_eq, comparator_25_eq, comparator_40_eq, comparator_55_eq);
  and and_9 (and_9_out, comparator_58_eq, comparator_11_eq, comparator_26_eq, comparator_41_eq, comparator_56_eq, comparator_12_eq, comparator_13_eq, comparator_14_eq, comparator_27_eq, comparator_57_eq, comparator_28_eq, comparator_29_eq, comparator_43_eq, comparator_44_eq, comparator_59_eq, comparator_15_eq, comparator_30_eq, comparator_45_eq, comparator_60_eq);
  Display1_Decoder display1_decoder_1 (
    .D(multiplexer_35_out), .C(multiplexer_50_out), .B(multiplexer_66_out), .A(multiplexer_90_out),
    .a_2(display1_decoder_1_a_2), .b_2(display1_decoder_1_b_2), .c_2(display1_decoder_1_c_2),
    .d_2(display1_decoder_1_d_2), .e(display1_decoder_1_e), .f(display1_decoder_1_f), .g(display1_decoder_1_g));
  Multiplexer multiplexer_96 (
    .in0(d_ff_71_q), .in1(priority_encoder_1_out[0]), .out(multiplexer_96_out), .sel(priority_encoder_1_gs),
    .en(and_1_out));
  Multiplexer multiplexer_97 (
    .in0(d_ff_72_q), .in1(d_ff_71_q), .out(multiplexer_97_out), .sel(priority_encoder_1_gs), .en(and_1_out));
  Multiplexer multiplexer_98 (
    .in0(d_ff_73_q), .in1(d_ff_72_q), .out(multiplexer_98_out), .sel(priority_encoder_1_gs), .en(and_1_out));
  Multiplexer multiplexer_99 (
    .in0(d_ff_74_q), .in1(d_ff_73_q), .out(multiplexer_99_out), .sel(priority_encoder_1_gs), .en(and_1_out));
  Multiplexer multiplexer_100 (
    .in0(d_ff_75_q), .in1(d_ff_74_q), .out(multiplexer_100_out), .sel(priority_encoder_1_gs), .en(and_1_out));
  or or_2 (or_2_out, and_7_out, and_9_out, and_8_out);

  // Notes on the sheet:
  //   Keypad
  //   Mode 0 = Admin
  //   Mode 1 = Check Pattern
  //   Select Pattern
  //   Display2
  //   O = Match
  //   N = Not Match
  //   Display1
endmodule

module Display2_Decoder (
  input  X,
  output a,
  output b,
  output c,
  output d,
  output e,
  output f,
  output g
);

  wire not_1_out;

  not not_1 (not_1_out, X);
  or or_1 (a, X, not_1_out);
  not not_2 (g, a);

  assign b = a;
  assign c = a;
  assign d = X;
  assign e = a;
  assign f = a;
endmodule

module Display1_Decoder (
  input  D,
  input  C,
  input  B,
  input  A,
  output a_2,
  output b_2,
  output c_2,
  output d_2,
  output e,
  output f,
  output g
);

  wire and_1_out, and_2_out, and_3_out, and_4_out, and_5_out, and_6_out, and_7_out, and_8_out, and_10_out,
       and_11_out, not_1_out, not_2_out, not_3_out, or_2_out, or_3_out, or_4_out;

  not not_1 (not_1_out, C);
  not not_2 (not_2_out, B);
  not not_3 (not_3_out, A);
  and and_1 (and_1_out, C, A);
  and and_2 (and_2_out, not_1_out, not_3_out);
  and and_3 (and_3_out, not_2_out, not_3_out);
  and and_4 (and_4_out, B, A);
  or or_1 (c_2, not_2_out, A, C);
  or or_2 (or_2_out, B, not_1_out);
  and and_5 (and_5_out, C, not_2_out, A);
  and and_6 (and_6_out, not_1_out, B);
  or or_3 (or_3_out, not_3_out, C);
  and and_7 (and_7_out, C, not_3_out);
  or or_4 (or_4_out, not_3_out, not_2_out);
  and and_8 (and_8_out, B, not_1_out);
  or or_5 (a_2, and_1_out, and_2_out, B, D);
  or or_6 (b_2, and_3_out, and_4_out, not_1_out);
  and and_9 (e, not_3_out, or_2_out);
  and and_10 (and_10_out, not_2_out, or_3_out);
  and and_11 (and_11_out, or_4_out, C);
  or or_7 (g, and_11_out, and_8_out, D);
  or or_8 (d_2, e, and_5_out, and_6_out, D);
  or or_9 (f, and_10_out, and_7_out, D);
endmodule
